// Logisim project Control_Avion.circ as structural Verilog: 13 circuits, main circuit main
module main (
);

  wire a_t, b, c, D, d_t, deco_complementario_1_s0, deco_complementario_1_s1, deco_complementario_1_s2,
       deco_elevadores_1_s1, deco_elevadores_1_s2, deco_elevadores_1_s3, \deco_timón_1_s1 ,
       \deco_timón_1_s2 , \deco_timón_1_s3 , e_t, f, g, S1, S2, S3, U;
  wire [1:0] A, E, T;
  wire [4:0] C1_AD, C1_AI, C1_E, C1_T, C2_AD, C2_AI, C2_E, C2_T, C3_AD, C3_AI, C3_E, C3_T, C4_AD, C4_AI,
       C4_E, C4_T;

  DotMatrix #(.matrixcols(4), .matrixrows(5)) dotmatrix_1 (.col0(C1_AI), .col1(C2_AI), .col2(C3_AI), .col3(C4_AI));
  Display_5x4 display_5x4_1 (.x(S1), .y(S2), .z(S3), .col1(C1_AI), .col2(C2_AI), .col3(C3_AI), .col4(C4_AI));
  Deco__Alerones deco_alerones_1 (.w(A[1]), .x(A[0]), .s1(S1), .s2(S2), .s3(S3));
  Joystick #(.bits(2)) joystick_1 (.x(A));  // open: y
  DotMatrix #(.matrixcols(4), .matrixrows(5)) dotmatrix_2 (.col0(C1_AD), .col1(C2_AD), .col2(C3_AD), .col3(C4_AD));
  Display_5x4 display_5x4_2 (
    .x(deco_complementario_1_s0), .y(deco_complementario_1_s1), .z(deco_complementario_1_s2), .col1(C1_AD),
    .col2(C2_AD), .col3(C3_AD), .col4(C4_AD));
  Deco_complementario deco_complementario_1 (
    .w(S1), .x(S2), .y(S3), .s0(deco_complementario_1_s0), .s1(deco_complementario_1_s1),
    .s2(deco_complementario_1_s2));
  _7_Segment_Display u_7_segment_display_1 (.g(g), .f(f), .a(a_t), .b(b), .e(e_t), .d(d_t), .c(c), .dp(1'b1));
  Button u_U (.out(U));
  Button u_D (.out(D));
  Speed_Display speed_display_1 (.U(U), .D(D), .a(a_t), .b(b), .c(c), .d_2(d_t), .e(e_t), .f(f), .g(g));
  DotMatrix #(.matrixcols(4), .matrixrows(5)) dotmatrix_3 (.col0(C1_T), .col1(C2_T), .col2(C3_T), .col3(C4_T));
  Display_5x4 display_5x4_3 (
    .x(\deco_timón_1_s1 ), .y(\deco_timón_1_s2 ), .z(\deco_timón_1_s3 ), .col1(C1_T), .col2(C2_T),
    .col3(C3_T), .col4(C4_T));
  \Deco_Timón  \deco_timón_1  (
    .x(T[1]), .y(T[0]), .s1(\deco_timón_1_s1 ), .s2(\deco_timón_1_s2 ), .s3(\deco_timón_1_s3 ));
  Joystick #(.bits(2)) joystick_2 (.x(T), .y(E));
  DotMatrix #(.matrixcols(4), .matrixrows(5)) dotmatrix_4 (.col0(C1_E), .col1(C2_E), .col2(C3_E), .col3(C4_E));
  Display_5x4 display_5x4_4 (
    .x(deco_elevadores_1_s1), .y(deco_elevadores_1_s2), .z(deco_elevadores_1_s3), .col1(C1_E), .col2(C2_E),
    .col3(C3_E), .col4(C4_E));
  Deco_Elevadores deco_elevadores_1 (
    .x(E[1]), .y(E[0]), .s1(deco_elevadores_1_s1), .s2(deco_elevadores_1_s2), .s3(deco_elevadores_1_s3));

  // Notes on the sheet:
  //   Izquierdo
  //   Alerones
  //   Derecho
  //   Velocidad
  //   Timón
  //   Elevadores
endmodule

module Control_Speed (
  input  v,
  input  w,
  input  x,
  input  y,
  input  z,
  output Ns2,
  output Ns1,
  output Ns0
);

  wire and_1_out, and_2_out, and_3_out, and_4_out, and_5_out, and_6_out, and_7_out, and_8_out, and_9_out,
       and_10_out, and_11_out, and_12_out, and_13_out, and_14_out, and_15_out, and_16_out, and_17_out,
       not_1_out, not_2_out, not_3_out, not_4_out, not_5_out, not_6_out, not_7_out, not_8_out, not_9_out,
       not_10_out, not_11_out, not_12_out, not_13_out, not_14_out, not_15_out, not_16_out, not_17_out,
       not_18_out;

  not not_1 (not_1_out, z);
  not not_2 (not_2_out, z);
  not not_3 (not_3_out, w);
  not not_4 (not_4_out, z);
  not not_5 (not_5_out, w);
  not not_6 (not_6_out, x);
  not not_7 (not_7_out, y);
  not not_8 (not_8_out, x);
  not not_9 (not_9_out, z);
  not not_10 (not_10_out, y);
  not not_11 (not_11_out, x);
  not not_12 (not_12_out, z);
  not not_13 (not_13_out, y);
  not not_14 (not_14_out, z);
  not not_15 (not_15_out, x);
  not not_16 (not_16_out, y);
  not not_17 (not_17_out, x);
  not not_18 (not_18_out, y);
  and and_1 (and_1_out, w, x, y, not_1_out);
  and and_2 (and_2_out, v, y);
  and and_3 (and_3_out, v, x);
  and and_4 (and_4_out, v, w);
  and and_5 (and_5_out, v, not_2_out);
  and and_6 (and_6_out, not_3_out, x, y, not_4_out);
  and and_7 (and_7_out, v, not_5_out, not_6_out, not_7_out, z);
  and and_8 (and_8_out, v, w, x);
  and and_9 (and_9_out, w, not_8_out, not_9_out);
  and and_10 (and_10_out, w, y, z);
  and and_11 (and_11_out, w, x, not_10_out);
  and and_12 (and_12_out, not_11_out, y, not_12_out);
  and and_13 (and_13_out, x, not_13_out, not_14_out);
  and and_14 (and_14_out, x, y, z);
  and and_15 (and_15_out, w, not_15_out, not_16_out, z);
  and and_16 (and_16_out, v, not_17_out, not_18_out, z);
  and and_17 (and_17_out, v, w, x, y);
  or or_1 (Ns2, and_1_out, and_2_out, and_3_out, and_4_out, and_5_out);
  or or_2 (Ns1, and_6_out, and_7_out, and_8_out, and_9_out, and_10_out, and_11_out);
  or or_3 (Ns0, and_12_out, and_13_out, and_14_out, and_15_out, and_16_out, and_17_out);
endmodule

module Speed (
  input  U,
  input  D,
  output [2:0] Ns
);

  wire clock_1_out;
  wire [2:0] control_speed_1_ns0;

  Control_Speed control_speed_1 (
    .v(Ns[2]), .w(Ns[1]), .x(Ns[0]), .y(U), .z(D), .Ns2(control_speed_1_ns0[2]),
    .Ns1(control_speed_1_ns0[1]), .Ns0(control_speed_1_ns0[0]));
  Clock clock_1 (.out(clock_1_out));
  Register #(.width(3)) register_1 (.D(control_speed_1_ns0), .Q(Ns), .clk(clock_1_out));  // open: en, clr
endmodule

module Speed_Display (
  input  U,
  input  D,
  output a,
  output b,
  output c,
  output d_2,
  output e,
  output f,
  output g
);

  wire and_1_out, and_2_out, and_3_out, and_4_out, and_5_out, and_6_out, and_7_out, and_8_out, and_9_out,
       and_10_out, and_11_out, and_12_out, and_13_out, and_14_out, and_15_out, and_16_out, not_1_out,
       not_2_out, not_3_out, not_4_out, not_5_out, not_6_out, not_7_out, not_8_out, not_9_out, not_10_out,
       not_11_out, not_12_out, not_13_out, not_14_out, not_15_out, not_16_out, not_17_out, not_18_out,
       not_19_out, not_20_out, not_21_out;
  wire [2:0] speed_1_ns;

  Speed speed_1 (.U(U), .D(D), .Ns(speed_1_ns));
  not not_1 (not_1_out, speed_1_ns[2]);
  not not_2 (not_2_out, speed_1_ns[0]);
  not not_3 (not_3_out, speed_1_ns[1]);
  not not_4 (not_4_out, speed_1_ns[0]);
  not not_5 (not_5_out, speed_1_ns[1]);
  not not_6 (not_6_out, speed_1_ns[2]);
  not not_7 (not_7_out, speed_1_ns[0]);
  not not_8 (not_8_out, speed_1_ns[2]);
  not not_9 (not_9_out, speed_1_ns[0]);
  not not_10 (not_10_out, speed_1_ns[1]);
  not not_11 (not_11_out, speed_1_ns[2]);
  not not_12 (not_12_out, speed_1_ns[0]);
  not not_13 (not_13_out, speed_1_ns[0]);
  not not_14 (not_14_out, speed_1_ns[1]);
  not not_15 (not_15_out, speed_1_ns[0]);
  not not_16 (not_16_out, speed_1_ns[1]);
  not not_17 (not_17_out, speed_1_ns[0]);
  not not_18 (not_18_out, speed_1_ns[2]);
  not not_19 (not_19_out, speed_1_ns[1]);
  not not_20 (not_20_out, speed_1_ns[0]);
  and and_1 (and_1_out, not_1_out, not_2_out);
  and and_2 (and_2_out, speed_1_ns[2], speed_1_ns[0]);
  not not_21 (not_21_out, speed_1_ns[2]);
  and and_3 (and_3_out, not_3_out, not_4_out);
  and and_4 (and_4_out, speed_1_ns[1], speed_1_ns[0]);
  or or_1 (c, not_5_out, speed_1_ns[0], speed_1_ns[2]);
  and and_5 (and_5_out, not_6_out, not_7_out);
  and and_6 (and_6_out, not_8_out, speed_1_ns[1]);
  and and_7 (and_7_out, speed_1_ns[1], not_9_out);
  and and_8 (and_8_out, speed_1_ns[2], not_10_out, speed_1_ns[0]);
  and and_9 (and_9_out, not_11_out, not_12_out);
  and and_10 (and_10_out, speed_1_ns[1], not_13_out);
  and and_11 (and_11_out, not_14_out, not_15_out);
  and and_12 (and_12_out, speed_1_ns[2], not_16_out);
  and and_13 (and_13_out, speed_1_ns[2], not_17_out);
  and and_14 (and_14_out, not_18_out, speed_1_ns[1]);
  and and_15 (and_15_out, speed_1_ns[2], not_19_out);
  and and_16 (and_16_out, speed_1_ns[2], not_20_out);
  or or_2 (a, and_1_out, speed_1_ns[1], and_2_out);
  or or_3 (b, not_21_out, and_3_out, and_4_out);
  or or_4 (d_2, and_5_out, and_6_out, and_7_out, and_8_out);
  or or_5 (e, and_9_out, and_10_out);
  or or_6 (f, and_11_out, and_12_out, and_13_out);
  or or_7 (g, and_14_out, and_15_out, and_16_out);
endmodule

// 1
module Led_1_13 (
  input  x,
  input  y,
  input  z,
  output a
);

  wire and_1_out, and_2_out, and_3_out, not_1_out, not_2_out, not_3_out;

  not not_1 (not_1_out, x);
  not not_2 (not_2_out, z);
  not not_3 (not_3_out, z);
  and and_1 (and_1_out, not_1_out, not_2_out);
  and and_2 (and_2_out, y, not_3_out);
  and and_3 (and_3_out, x, y);
  or or_1 (a, and_1_out, and_2_out, and_3_out);
endmodule

// 3
module Led_3_10_11 (
  input  x,
  input  y,
  input  z,
  output a
);

  and and_1 (a, y, z);
endmodule

// 4
module Led_4_16 (
  input  x,
  input  y,
  input  z,
  output a
);

  wire and_1_out, and_2_out, not_1_out, not_2_out, not_3_out, not_4_out;

  not not_1 (not_1_out, x);
  not not_2 (not_2_out, y);
  not not_3 (not_3_out, z);
  not not_4 (not_4_out, x);
  and and_1 (and_1_out, not_1_out, not_2_out, not_3_out);
  and and_2 (and_2_out, not_4_out, y, z);
  or or_1 (a, and_1_out, and_2_out);
endmodule

// 5
module Led_5_9_17 (
  input  x,
  input  y,
  input  z,
  output a
);

  wire and_1_out, not_1_out, not_2_out;

  not not_1 (not_1_out, x);
  not not_2 (not_2_out, z);
  and and_1 (and_1_out, not_1_out, not_2_out);
  or or_1 (a, and_1_out, y);
endmodule

// 5 x 4
module Display_5x4 (
  input  x,
  input  y,
  input  z,
  output [4:0] col1,
  output [4:0] col2,
  output [4:0] col3,
  output [4:0] col4
);

  wire and_1_out, and_2_out, and_3_out, and_4_out, and_5_out, and_6_out, and_7_out, and_9_out, and_10_out,
       and_11_out, and_12_out, and_13_out, and_14_out, and_15_out, and_16_out, and_17_out, not_1_out,
       not_2_out, not_3_out, not_4_out, not_5_out, not_6_out, not_7_out, not_8_out, not_9_out, not_10_out,
       not_11_out, not_12_out, not_13_out, not_14_out, not_15_out, not_16_out, not_17_out, not_18_out,
       not_19_out, not_20_out, not_21_out, not_22_out, not_23_out, not_24_out;

  Led_5_9_17 led_5_9_17_1 (.x(x), .y(y), .z(z), .a(col1[3]));
  Led_5_9_17 led_5_9_17_2 (.x(x), .y(y), .z(z), .a(col1[2]));
  Led_1_13 led_1_13_1 (.x(x), .y(y), .z(z), .a(col1[1]));
  Led_5_9_17 led_5_9_17_3 (.x(x), .y(y), .z(z), .a(col1[0]));
  Led_1_13 led_1_13_2 (.x(x), .y(y), .z(z), .a(col1[4]));
  not not_1 (not_1_out, x);
  not not_2 (not_2_out, x);
  not not_3 (not_3_out, y);
  not not_4 (not_4_out, z);
  not not_5 (not_5_out, x);
  not not_6 (not_6_out, z);
  and and_1 (and_1_out, not_1_out, y);
  and and_2 (and_2_out, y, z);
  Led_3_10_11 led_3_10_11_1 (.x(x), .y(y), .z(z), .a(col2[2]));
  and and_3 (and_3_out, not_2_out, not_3_out, not_4_out);
  and and_4 (and_4_out, not_5_out, y);
  and and_5 (and_5_out, y, not_6_out);
  or or_1 (col2[4], and_1_out, and_2_out);
  or or_2 (col2[0], and_3_out, and_4_out, and_5_out);
  not not_7 (not_7_out, x);
  not not_8 (not_8_out, z);
  Led_3_10_11 led_3_10_11_2 (.x(x), .y(y), .z(z), .a(col3[4]));
  not not_9 (not_9_out, x);
  not not_10 (not_10_out, z);
  Led_3_10_11 led_3_10_11_3 (.x(x), .y(y), .z(z), .a(col3[2]));
  and and_6 (and_6_out, not_7_out, y, not_8_out);
  and and_7 (and_7_out, x, y, z);
  not not_11 (not_11_out, x);
  not not_12 (not_12_out, y);
  not not_13 (not_13_out, z);
  not not_14 (not_14_out, x);
  not not_15 (not_15_out, z);
  and and_8 (col3[3], not_9_out, y, not_10_out);
  or or_3 (col3[1], and_6_out, and_7_out);
  and and_9 (and_9_out, not_11_out, not_12_out, not_13_out);
  and and_10 (and_10_out, not_14_out, y, z);
  and and_11 (and_11_out, x, y, not_15_out);
  or or_4 (col3[0], and_9_out, and_10_out, and_11_out);
  Led_4_16 led_4_16_1 (.x(x), .y(y), .z(z), .a(col4[4]));
  not not_16 (not_16_out, x);
  not not_17 (not_17_out, y);
  not not_18 (not_18_out, z);
  not not_19 (not_19_out, x);
  not not_20 (not_20_out, z);
  not not_21 (not_21_out, x);
  Led_4_16 led_4_16_2 (.x(x), .y(y), .z(z), .a(col4[1]));
  not not_22 (not_22_out, x);
  not not_23 (not_23_out, y);
  not not_24 (not_24_out, z);
  and and_12 (and_12_out, not_16_out, not_17_out, not_18_out);
  and and_13 (and_13_out, x, y, z);
  and and_14 (and_14_out, not_19_out, not_20_out);
  and and_15 (and_15_out, not_21_out, y);
  and and_16 (and_16_out, not_22_out, not_23_out, not_24_out);
  and and_17 (and_17_out, x, y);
  or or_5 (col4[3], and_12_out, and_13_out);
  or or_6 (col4[2], and_14_out, and_15_out);
  or or_7 (col4[0], and_16_out, and_17_out);

  assign {col2[3], col2[1]} = 2'b00;

  // Notes on the sheet:
  //   Led 1
  //   Led 5
  //   Led 9
  //   Led 13
  //   Led 17
  //   Led 2
  //   Led 6
  //   Led 10
  //   Led 14
  //   Led 18
  //   Led 3
  //   Led 7
  //   Led 11
  //   Led 15
  //   Led 19
  //   Led 4
  //   Led 8
  //   Led 12
  //   Led 16
  //   Led 20
endmodule

// DA
module Deco__Alerones (
  input  w,
  input  x,
  output s1,
  output s2,
  output s3
);

  not not_1 (s3, x);

  assign s1 = 1'b0;
  assign s2 = w;
endmodule

// DC
module Deco_complementario (
  input  w,
  input  x,
  input  y,
  output s0,
  output s1,
  output s2
);

  wire not_1_out;

  not not_1 (not_1_out, x);
  or or_1 (s1, not_1_out, y);

  assign s0 = 1'b0;
  assign s2 = y;
endmodule

// DT
module \Deco_Timón  (
  input  x,
  input  y,
  output s1,
  output s2,
  output s3
);


  assign s1 = y;
  assign s2 = 1'b1;
  assign s3 = x;
endmodule

// DE
module Deco_Elevadores (
  input  x,
  input  y,
  output s1,
  output s2,
  output s3
);

  not not_1 (s3, y);

  assign s1 = 1'b0;
  assign s2 = x;
endmodule
