// Logisim project Procesador.circ as structural Verilog: 16 circuits, main circuit Procesador
module Sumador_1bit (
  input  A,
  input  B,
  input  Cin,
  output Cout,
  output R
);

  wire and_1_out, and_2_out, and_3_out, and_4_out, and_5_out, and_6_out, and_7_out, not_1_out, not_2_out,
       not_3_out, not_4_out, not_5_out, not_6_out;

  and and_1 (and_1_out, B, Cin);
  and and_2 (and_2_out, A, Cin);
  and and_3 (and_3_out, A, B);
  not not_1 (not_1_out, A);
  not not_2 (not_2_out, B);
  not not_3 (not_3_out, A);
  not not_4 (not_4_out, Cin);
  not not_5 (not_5_out, B);
  not not_6 (not_6_out, Cin);
  or or_1 (Cout, and_1_out, and_2_out, and_3_out);
  and and_4 (and_4_out, not_1_out, not_2_out, Cin);
  and and_5 (and_5_out, not_3_out, B, not_4_out);
  and and_6 (and_6_out, A, not_5_out, not_6_out);
  and and_7 (and_7_out, A, B, Cin);
  or or_2 (R, and_4_out, and_5_out, and_6_out, and_7_out);
endmodule

module ALU_1_bit (
  input  [2:0] ALU_operation,
  input  A,
  input  B,
  input  Cin,
  input  binv,
  output R,
  output Cout
);

  wire and_1_out, multiplexer_1_out, not_1_out, not_2_out, or_1_out, Sumador_r;

  not not_1 (not_1_out, B);
  Multiplexer multiplexer_1 (.in0(B), .in1(not_1_out), .out(multiplexer_1_out), .sel(binv));  // open: en
  and and_1 (and_1_out, A, B);
  or or_1 (or_1_out, A, B);
  not not_2 (not_2_out, or_1_out);
  Sumador_1bit Sumador (.A(A), .B(multiplexer_1_out), .Cin(Cin), .Cout(Cout), .R(Sumador_r));
  Multiplexer #(.select(3)) multiplexer_2 (
    .in0(and_1_out), .in1(Sumador_r), .in3(Sumador_r), .in4(not_2_out), .in6(or_1_out), .in7(Sumador_r),
    .out(R), .sel(ALU_operation));  // open: in2, in5, en
endmodule

module Sumador_1bit_overflow (
  input  A,
  input  B,
  input  Cin,
  output Cout,
  output S,
  output Overflow
);

  wire and_1_out, and_2_out, and_3_out, and_4_out, and_5_out, and_6_out, and_7_out, and_8_out, and_9_out,
       not_1_out, not_2_out, not_3_out, not_4_out, not_5_out, not_6_out, not_7_out, not_8_out, not_9_out;

  and and_1 (and_1_out, B, Cin);
  and and_2 (and_2_out, A, Cin);
  and and_3 (and_3_out, A, B);
  not not_1 (not_1_out, A);
  not not_2 (not_2_out, B);
  not not_3 (not_3_out, A);
  not not_4 (not_4_out, Cin);
  not not_5 (not_5_out, B);
  not not_6 (not_6_out, Cin);
  not not_7 (not_7_out, A);
  not not_8 (not_8_out, B);
  not not_9 (not_9_out, Cin);
  or or_1 (Cout, and_1_out, and_2_out, and_3_out);
  and and_4 (and_4_out, not_1_out, not_2_out, Cin);
  and and_5 (and_5_out, not_3_out, B, not_4_out);
  and and_6 (and_6_out, A, not_5_out, not_6_out);
  and and_7 (and_7_out, A, B, Cin);
  and and_8 (and_8_out, not_7_out, not_8_out, Cin);
  and and_9 (and_9_out, A, B, not_9_out);
  or or_2 (S, and_4_out, and_5_out, and_6_out, and_7_out);
  or or_3 (Overflow, and_8_out, and_9_out);
endmodule

module ALU_1bit_overflow (
  input  [2:0] ALU_operation,
  input  A,
  input  B,
  input  Cin,
  input  binv,
  output R,
  output Cout,
  output Overflow
);

  wire and_1_out, multiplexer_1_out, not_1_out, not_2_out, or_1_out, sumador_1bit_overflow_1_s;

  not not_1 (not_1_out, B);
  Multiplexer multiplexer_1 (.in0(B), .in1(not_1_out), .out(multiplexer_1_out), .sel(binv));  // open: en
  and and_1 (and_1_out, A, B);
  or or_1 (or_1_out, A, B);
  not not_2 (not_2_out, or_1_out);
  Sumador_1bit_overflow sumador_1bit_overflow_1 (
    .A(A), .B(multiplexer_1_out), .Cin(Cin), .Cout(Cout), .S(sumador_1bit_overflow_1_s), .Overflow(Overflow));
  Multiplexer #(.select(3)) multiplexer_2 (
    .in0(and_1_out), .in1(sumador_1bit_overflow_1_s), .in3(sumador_1bit_overflow_1_s), .in4(not_2_out),
    .in6(or_1_out), .in7(sumador_1bit_overflow_1_s), .out(R), .sel(ALU_operation));  // open: in2, in5, en
endmodule

// ALU
module ALU_32_bits (
  input  [2:0] ALU_operacion,
  input  [31:0] A,
  input  [31:0] B,
  output Cero,
  output [31:0] ALU_Result
);

  wire _0, _1, _2, _3, _4, _5, _6, _7, _8, _9, _10, _11, _12, _13, _14, _15, _16, _17, _18, _19, _20, _21,
       _22, _23, _24, _25, _26, _27, _28, _29, _30, _31, alu_1_bit_1_cout, alu_1_bit_2_cout,
       alu_1_bit_3_cout, alu_1_bit_4_cout, alu_1_bit_5_cout, alu_1_bit_6_cout, alu_1_bit_7_cout,
       alu_1_bit_8_cout, alu_1_bit_9_cout, alu_1_bit_10_cout, alu_1_bit_11_cout, alu_1_bit_12_cout,
       alu_1_bit_13_cout, alu_1_bit_14_cout, alu_1_bit_15_cout, alu_1_bit_16_cout, alu_1_bit_17_cout,
       alu_1_bit_18_cout, alu_1_bit_19_cout, alu_1_bit_20_cout, alu_1_bit_21_cout, alu_1_bit_22_cout,
       alu_1_bit_23_cout, alu_1_bit_24_cout, alu_1_bit_25_cout, alu_1_bit_26_cout, alu_1_bit_27_cout,
       alu_1_bit_28_cout, alu_1_bit_29_cout, alu_1_bit_30_cout, alu_1_bit_31_cout, alu_1bit_overflow_1_cout,
       alu_1bit_overflow_1_overflow, multiplexer_1_out, slt;

  Multiplexer #(.select(3)) multiplexer_1 (
    .in0(1'b0), .in1(1'b1), .in2(1'b0), .in3(1'b0), .in4(1'b0), .in5(1'b0), .in6(1'b0), .in7(1'b1),
    .out(multiplexer_1_out), .sel(ALU_operacion));  // open: en
  ALU_1_bit alu_1_bit_1 (
    .A(A[0]), .B(B[0]), .Cin(multiplexer_1_out), .binv(multiplexer_1_out), .ALU_operation(ALU_operacion),
    .R(_0), .Cout(alu_1_bit_1_cout));
  ALU_1_bit alu_1_bit_2 (
    .A(A[1]), .B(B[1]), .Cin(alu_1_bit_1_cout), .binv(multiplexer_1_out), .ALU_operation(ALU_operacion),
    .R(_1), .Cout(alu_1_bit_2_cout));
  ALU_1_bit alu_1_bit_3 (
    .A(A[2]), .B(B[2]), .Cin(alu_1_bit_2_cout), .binv(multiplexer_1_out), .ALU_operation(ALU_operacion),
    .R(_2), .Cout(alu_1_bit_3_cout));
  ALU_1_bit alu_1_bit_4 (
    .A(A[3]), .B(B[3]), .Cin(alu_1_bit_3_cout), .binv(multiplexer_1_out), .ALU_operation(ALU_operacion),
    .R(_3), .Cout(alu_1_bit_4_cout));
  ALU_1_bit alu_1_bit_5 (
    .A(A[4]), .B(B[4]), .Cin(alu_1_bit_4_cout), .binv(multiplexer_1_out), .ALU_operation(ALU_operacion),
    .R(_4), .Cout(alu_1_bit_5_cout));
  ALU_1_bit alu_1_bit_6 (
    .A(A[5]), .B(B[5]), .Cin(alu_1_bit_5_cout), .binv(multiplexer_1_out), .ALU_operation(ALU_operacion),
    .R(_5), .Cout(alu_1_bit_6_cout));
  ALU_1_bit alu_1_bit_7 (
    .A(A[6]), .B(B[6]), .Cin(alu_1_bit_6_cout), .binv(multiplexer_1_out), .ALU_operation(ALU_operacion),
    .R(_6), .Cout(alu_1_bit_7_cout));
  ALU_1_bit alu_1_bit_8 (
    .A(A[7]), .B(B[7]), .Cin(alu_1_bit_7_cout), .binv(multiplexer_1_out), .ALU_operation(ALU_operacion),
    .R(_7), .Cout(alu_1_bit_8_cout));
  ALU_1_bit alu_1_bit_9 (
    .A(A[8]), .B(B[8]), .Cin(alu_1_bit_8_cout), .binv(multiplexer_1_out), .ALU_operation(ALU_operacion),
    .R(_8), .Cout(alu_1_bit_9_cout));
  ALU_1_bit alu_1_bit_10 (
    .A(A[9]), .B(B[9]), .Cin(alu_1_bit_9_cout), .binv(multiplexer_1_out), .ALU_operation(ALU_operacion),
    .R(_9), .Cout(alu_1_bit_10_cout));
  ALU_1_bit alu_1_bit_11 (
    .A(A[10]), .B(B[10]), .Cin(alu_1_bit_10_cout), .binv(multiplexer_1_out), .ALU_operation(ALU_operacion),
    .R(_10), .Cout(alu_1_bit_11_cout));
  ALU_1_bit alu_1_bit_12 (
    .A(A[11]), .B(B[11]), .Cin(alu_1_bit_11_cout), .binv(multiplexer_1_out), .ALU_operation(ALU_operacion),
    .R(_11), .Cout(alu_1_bit_12_cout));
  ALU_1_bit alu_1_bit_13 (
    .A(A[12]), .B(B[12]), .Cin(alu_1_bit_12_cout), .binv(multiplexer_1_out), .ALU_operation(ALU_operacion),
    .R(_12), .Cout(alu_1_bit_13_cout));
  ALU_1_bit alu_1_bit_14 (
    .A(A[13]), .B(B[13]), .Cin(alu_1_bit_13_cout), .binv(multiplexer_1_out), .ALU_operation(ALU_operacion),
    .R(_13), .Cout(alu_1_bit_14_cout));
  ALU_1_bit alu_1_bit_15 (
    .A(A[14]), .B(B[14]), .Cin(alu_1_bit_14_cout), .binv(multiplexer_1_out), .ALU_operation(ALU_operacion),
    .R(_14), .Cout(alu_1_bit_15_cout));
  ALU_1_bit alu_1_bit_16 (
    .A(A[15]), .B(B[15]), .Cin(alu_1_bit_15_cout), .binv(multiplexer_1_out), .ALU_operation(ALU_operacion),
    .R(_15), .Cout(alu_1_bit_16_cout));
  ALU_1_bit alu_1_bit_17 (
    .A(A[16]), .B(B[16]), .Cin(alu_1_bit_16_cout), .binv(multiplexer_1_out), .ALU_operation(ALU_operacion),
    .R(_16), .Cout(alu_1_bit_17_cout));
  ALU_1_bit alu_1_bit_18 (
    .A(A[17]), .B(B[17]), .Cin(alu_1_bit_17_cout), .binv(multiplexer_1_out), .ALU_operation(ALU_operacion),
    .R(_17), .Cout(alu_1_bit_18_cout));
  ALU_1_bit alu_1_bit_19 (
    .A(A[18]), .B(B[18]), .Cin(alu_1_bit_18_cout), .binv(multiplexer_1_out), .ALU_operation(ALU_operacion),
    .R(_18), .Cout(alu_1_bit_19_cout));
  ALU_1_bit alu_1_bit_20 (
    .A(A[19]), .B(B[19]), .Cin(alu_1_bit_19_cout), .binv(multiplexer_1_out), .ALU_operation(ALU_operacion),
    .R(_19), .Cout(alu_1_bit_20_cout));
  ALU_1_bit alu_1_bit_21 (
    .A(A[20]), .B(B[20]), .Cin(alu_1_bit_20_cout), .binv(multiplexer_1_out), .ALU_operation(ALU_operacion),
    .R(_20), .Cout(alu_1_bit_21_cout));
  ALU_1_bit alu_1_bit_22 (
    .A(A[21]), .B(B[21]), .Cin(alu_1_bit_21_cout), .binv(multiplexer_1_out), .ALU_operation(ALU_operacion),
    .R(_21), .Cout(alu_1_bit_22_cout));
  ALU_1_bit alu_1_bit_23 (
    .A(A[22]), .B(B[22]), .Cin(alu_1_bit_22_cout), .binv(multiplexer_1_out), .ALU_operation(ALU_operacion),
    .R(_22), .Cout(alu_1_bit_23_cout));
  ALU_1_bit alu_1_bit_24 (
    .A(A[23]), .B(B[23]), .Cin(alu_1_bit_23_cout), .binv(multiplexer_1_out), .ALU_operation(ALU_operacion),
    .R(_23), .Cout(alu_1_bit_24_cout));
  ALU_1_bit alu_1_bit_25 (
    .A(A[24]), .B(B[24]), .Cin(alu_1_bit_24_cout), .binv(multiplexer_1_out), .ALU_operation(ALU_operacion),
    .R(_24), .Cout(alu_1_bit_25_cout));
  ALU_1_bit alu_1_bit_26 (
    .A(A[25]), .B(B[25]), .Cin(alu_1_bit_25_cout), .binv(multiplexer_1_out), .ALU_operation(ALU_operacion),
    .R(_25), .Cout(alu_1_bit_26_cout));
  ALU_1_bit alu_1_bit_27 (
    .A(A[26]), .B(B[26]), .Cin(alu_1_bit_26_cout), .binv(multiplexer_1_out), .ALU_operation(ALU_operacion),
    .R(_26), .Cout(alu_1_bit_27_cout));
  ALU_1_bit alu_1_bit_28 (
    .A(A[27]), .B(B[27]), .Cin(alu_1_bit_27_cout), .binv(multiplexer_1_out), .ALU_operation(ALU_operacion),
    .R(_27), .Cout(alu_1_bit_28_cout));
  ALU_1_bit alu_1_bit_29 (
    .A(A[28]), .B(B[28]), .Cin(alu_1_bit_28_cout), .binv(multiplexer_1_out), .ALU_operation(ALU_operacion),
    .R(_28), .Cout(alu_1_bit_29_cout));
  ALU_1_bit alu_1_bit_30 (
    .A(A[29]), .B(B[29]), .Cin(alu_1_bit_29_cout), .binv(multiplexer_1_out), .ALU_operation(ALU_operacion),
    .R(_29), .Cout(alu_1_bit_30_cout));
  ALU_1_bit alu_1_bit_31 (
    .A(A[30]), .B(B[30]), .Cin(alu_1_bit_30_cout), .binv(multiplexer_1_out), .ALU_operation(ALU_operacion),
    .R(_30), .Cout(alu_1_bit_31_cout));
  ALU_1bit_overflow alu_1bit_overflow_1 (
    .A(A[31]), .B(B[31]), .Cin(alu_1_bit_31_cout), .binv(multiplexer_1_out), .ALU_operation(ALU_operacion),
    .R(_31), .Cout(alu_1bit_overflow_1_cout), .Overflow(alu_1bit_overflow_1_overflow));
  Multiplexer multiplexer_2 (
    .in0(_31), .in1(alu_1bit_overflow_1_cout), .out(slt), .sel(alu_1bit_overflow_1_overflow));  // open: en
  Multiplexer #(.select(3), .width(32)) multiplexer_3 (
    .in0({_31, _30, _29, _28, _27, _26, _25, _24, _23, _22, _21, _20, _19, _18, _17, _16, _15, _14, _13, _12, _11, _10, _9, _8, _7, _6, _5, _4, _3, _2, _1, _0}),
    .in1({_31, _30, _29, _28, _27, _26, _25, _24, _23, _22, _21, _20, _19, _18, _17, _16, _15, _14, _13, _12, _11, _10, _9, _8, _7, _6, _5, _4, _3, _2, _1, _0}),
    .in3({_31, _30, _29, _28, _27, _26, _25, _24, _23, _22, _21, _20, _19, _18, _17, _16, _15, _14, _13, _12, _11, _10, _9, _8, _7, _6, _5, _4, _3, _2, _1, _0}),
    .in4({_31, _30, _29, _28, _27, _26, _25, _24, _23, _22, _21, _20, _19, _18, _17, _16, _15, _14, _13, _12, _11, _10, _9, _8, _7, _6, _5, _4, _3, _2, _1, _0}),
    .in6({_31, _30, _29, _28, _27, _26, _25, _24, _23, _22, _21, _20, _19, _18, _17, _16, _15, _14, _13, _12, _11, _10, _9, _8, _7, _6, _5, _4, _3, _2, _1, _0}),
    .in7({{31{1'b0}}, slt}), .out(ALU_Result), .sel(ALU_operacion));  // open: in2, in5, en
  nor nor_1 (Cero, ALU_Result[0], ALU_Result[1], ALU_Result[2], ALU_Result[3], ALU_Result[4], ALU_Result[5], ALU_Result[6], ALU_Result[7], ALU_Result[8], ALU_Result[9], ALU_Result[10], ALU_Result[11], ALU_Result[12], ALU_Result[13], ALU_Result[14], ALU_Result[15], ALU_Result[16], ALU_Result[17], ALU_Result[18], ALU_Result[19], ALU_Result[20], ALU_Result[21], ALU_Result[22], ALU_Result[23], ALU_Result[24], ALU_Result[25], ALU_Result[26], ALU_Result[27], ALU_Result[28], ALU_Result[29], ALU_Result[30], ALU_Result[31]);

  // Other names for the same wires on the sheet: Op[2:0] = ALU_operacion;
  //   Resultado[31:0] = {_31, _30, _29, _28, _27, _26, _25, _24, _23, _22, _21, _20, _19, _18, _17, _16, _15, _14, _13, _12, _11, _10, _9, _8, _7, _6, _5, _4, _3, _2, _1, _0}
endmodule

module Control (
  input  [5:0] Op_Code,
  output RegDst,
  output ALUScr,
  output MemtoReg,
  output RegWrite,
  output MemRead,
  output MemWrite,
  output Branch,
  output [1:0] ALU_Op,
  output jump,
  output link
);

  wire and_3_out, and_4_out, not_1_out, not_2_out, not_3_out, not_4_out, not_5_out, not_6_out, not_7_out,
       not_8_out, not_9_out, not_10_out, not_11_out;

  not not_1 (not_1_out, Op_Code[3]);
  not not_2 (not_2_out, Op_Code[1]);
  or or_1 (ALUScr, Op_Code[1], Op_Code[3]);
  not not_3 (not_3_out, Op_Code[2]);
  not not_4 (not_4_out, Op_Code[1]);
  not not_5 (not_5_out, Op_Code[3]);
  not not_6 (not_6_out, Op_Code[3]);
  and and_1 (MemWrite, Op_Code[5], Op_Code[3]);
  not not_7 (not_7_out, Op_Code[3]);
  not not_8 (not_8_out, Op_Code[2]);
  not not_9 (not_9_out, Op_Code[1]);
  not not_10 (not_10_out, Op_Code[5]);
  not not_11 (not_11_out, Op_Code[5]);
  and and_2 (RegDst, not_1_out, not_2_out);
  and and_3 (and_3_out, not_3_out, not_4_out);
  and and_4 (and_4_out, not_5_out, Op_Code[0]);
  and and_5 (MemRead, Op_Code[5], not_6_out);
  and and_6 (ALU_Op[1], not_7_out, not_8_out, not_9_out);
  and and_7 (jump, not_10_out, Op_Code[1]);
  and and_8 (link, not_11_out, Op_Code[0]);
  or or_2 (RegWrite, and_3_out, and_4_out);

  assign ALU_Op[0] = Op_Code[2];
  assign Branch = Op_Code[2];
  assign MemtoReg = Op_Code[1];
endmodule

module ALU_Control (
  input  [1:0] OP,
  input  [5:0] Funcion,
  output [2:0] ALU_operation
);

  wire and_1_out, and_2_out, not_2_out, not_3_out, not_4_out;
  wire [1:1] not_1_out;
  wire [2:0] not_5_out;

  not not_1 (not_1_out[1], OP[0]);
  or or_1 (not_5_out[2], Funcion[0], Funcion[3]);
  not not_2 (not_2_out, Funcion[2]);
  not not_3 (not_3_out, Funcion[1]);
  not not_4 (not_4_out, Funcion[1]);
  not not_5 (not_5_out[0], Funcion[2]);
  and and_1 (and_1_out, not_2_out, not_3_out);
  or or_2 (not_5_out[1], and_1_out, and_2_out, Funcion[3]);
  and and_2 (and_2_out, not_4_out, Funcion[0]);
  Multiplexer #(.width(3)) multiplexer_1 (
    .in0({1'b0, not_1_out[1], 1'b1}), .in1(not_5_out), .out(ALU_operation), .sel(OP[1]));  // open: en

  // Other names for the same wires on the sheet: Funcion_t = OP[1]
endmodule

module Banco_de_Registros (
  input  [4:0] Read_Register_1,
  input  [4:0] Read_Register_2,
  input  [4:0] Write_Reg,
  input  [31:0] Write_Data,
  input  Clock,
  input  Reg_Write,
  input  Reset,
  output [31:0] Read_Data_1,
  output [31:0] Read_Data_2
);

  wire Clk, decoder_1_out0, decoder_1_out1, decoder_1_out2, decoder_1_out3, decoder_1_out4, decoder_1_out5,
       decoder_1_out6, decoder_1_out7, decoder_1_out8, decoder_1_out9, decoder_1_out10, decoder_1_out11,
       decoder_1_out12, decoder_1_out13, decoder_1_out14, decoder_1_out15, decoder_1_out16, decoder_1_out17,
       decoder_1_out18, decoder_1_out19, decoder_1_out20, decoder_1_out21, decoder_1_out22, decoder_1_out23,
       decoder_1_out24, decoder_1_out25, decoder_1_out26, decoder_1_out27, decoder_1_out28, decoder_1_out29,
       decoder_1_out30, decoder_1_out31;
  wire [31:0] _0, _1, _2, _3, _4, _5, _6, _7, _8, _9, _10, _11, _12, _13, _14, _15, _16, _17, _18, _19, _20,
       _21, _22, _23, _24, _25, _26, _27, _28, _29, _30, _31;

  and and_1 (Clk, Clock, Reg_Write);
  Decoder #(.select(5)) decoder_1 (
    .out0(decoder_1_out0), .out1(decoder_1_out1), .out2(decoder_1_out2), .out3(decoder_1_out3),
    .out4(decoder_1_out4), .out5(decoder_1_out5), .out6(decoder_1_out6), .out7(decoder_1_out7),
    .out8(decoder_1_out8), .out9(decoder_1_out9), .out10(decoder_1_out10), .out11(decoder_1_out11),
    .out12(decoder_1_out12), .out13(decoder_1_out13), .out14(decoder_1_out14), .out15(decoder_1_out15),
    .out16(decoder_1_out16), .out17(decoder_1_out17), .out18(decoder_1_out18), .out19(decoder_1_out19),
    .out20(decoder_1_out20), .out21(decoder_1_out21), .out22(decoder_1_out22), .out23(decoder_1_out23),
    .out24(decoder_1_out24), .out25(decoder_1_out25), .out26(decoder_1_out26), .out27(decoder_1_out27),
    .out28(decoder_1_out28), .out29(decoder_1_out29), .out30(decoder_1_out30), .out31(decoder_1_out31),
    .sel(Write_Reg));  // open: en
  Register #(.width(32)) Szero (.D({32{1'b0}}), .en(decoder_1_out0), .Q(_0), .clk(Clk), .clr(Reset));
  Register #(.width(32)) v0 (.D(Write_Data), .en(decoder_1_out2), .Q(_2), .clk(Clk), .clr(Reset));
  Register #(.width(32)) a0 (.D(Write_Data), .en(decoder_1_out4), .Q(_4), .clk(Clk), .clr(Reset));
  Register #(.width(32)) a2 (.D(Write_Data), .en(decoder_1_out6), .Q(_6), .clk(Clk), .clr(Reset));
  Register #(.width(32)) t0 (.D(Write_Data), .en(decoder_1_out8), .Q(_8), .clk(Clk), .clr(Reset));
  Register #(.width(32)) t2 (.D(Write_Data), .en(decoder_1_out10), .Q(_10), .clk(Clk), .clr(Reset));
  Register #(.width(32)) t4 (.D(Write_Data), .en(decoder_1_out12), .Q(_12), .clk(Clk), .clr(Reset));
  Register #(.width(32)) t6 (.D(Write_Data), .en(decoder_1_out14), .Q(_14), .clk(Clk), .clr(Reset));
  Register #(.width(32)) s0 (.D(Write_Data), .en(decoder_1_out16), .Q(_16), .clk(Clk), .clr(Reset));
  Register #(.width(32)) s2 (.D(Write_Data), .en(decoder_1_out18), .Q(_18), .clk(Clk), .clr(Reset));
  Register #(.width(32)) s4 (.D(Write_Data), .en(decoder_1_out20), .Q(_20), .clk(Clk), .clr(Reset));
  Register #(.width(32)) s6 (.D(Write_Data), .en(decoder_1_out22), .Q(_22), .clk(Clk), .clr(Reset));
  Register #(.width(32)) t8 (.D(Write_Data), .en(decoder_1_out24), .Q(_24), .clk(Clk), .clr(Reset));
  Register #(.width(32)) k0 (.D(Write_Data), .en(decoder_1_out26), .Q(_26), .clk(Clk), .clr(Reset));
  Register #(.width(32)) gp (.D(Write_Data), .en(decoder_1_out28), .Q(_28), .clk(Clk), .clr(Reset));
  Register #(.width(32)) fp (.D(Write_Data), .en(decoder_1_out30), .Q(_30), .clk(Clk), .clr(Reset));
  Register #(.width(32)) at (.D(Write_Data), .en(decoder_1_out1), .Q(_1), .clk(Clk), .clr(Reset));
  Register #(.width(32)) v1 (.D(Write_Data), .en(decoder_1_out3), .Q(_3), .clk(Clk), .clr(Reset));
  Register #(.width(32)) a1 (.D(Write_Data), .en(decoder_1_out5), .Q(_5), .clk(Clk), .clr(Reset));
  Register #(.width(32)) a3 (.D(Write_Data), .en(decoder_1_out7), .Q(_7), .clk(Clk), .clr(Reset));
  Register #(.width(32)) t1 (.D(Write_Data), .en(decoder_1_out9), .Q(_9), .clk(Clk), .clr(Reset));
  Register #(.width(32)) t3 (.D(Write_Data), .en(decoder_1_out11), .Q(_11), .clk(Clk), .clr(Reset));
  Register #(.width(32)) t5 (.D(Write_Data), .en(decoder_1_out13), .Q(_13), .clk(Clk), .clr(Reset));
  Register #(.width(32)) t7 (.D(Write_Data), .en(decoder_1_out15), .Q(_15), .clk(Clk), .clr(Reset));
  Register #(.width(32)) s1 (.D(Write_Data), .en(decoder_1_out17), .Q(_17), .clk(Clk), .clr(Reset));
  Register #(.width(32)) s3 (.D(Write_Data), .en(decoder_1_out19), .Q(_19), .clk(Clk), .clr(Reset));
  Register #(.width(32)) s5 (.D(Write_Data), .en(decoder_1_out21), .Q(_21), .clk(Clk), .clr(Reset));
  Register #(.width(32)) s7 (.D(Write_Data), .en(decoder_1_out23), .Q(_23), .clk(Clk), .clr(Reset));
  Register #(.width(32)) t9 (.D(Write_Data), .en(decoder_1_out25), .Q(_25), .clk(Clk), .clr(Reset));
  Register #(.width(32)) k1 (.D(Write_Data), .en(decoder_1_out27), .Q(_27), .clk(Clk), .clr(Reset));
  Register #(.width(32)) sp (.D(Write_Data), .en(decoder_1_out29), .Q(_29), .clk(Clk), .clr(Reset));
  Register #(.width(32)) ra (.D(Write_Data), .en(decoder_1_out31), .Q(_31), .clk(Clk), .clr(Reset));
  Multiplexer #(.select(5), .width(32)) multiplexer_1 (
    .in0(_0), .in1(_1), .in2(_2), .in3(_3), .in4(_4), .in5(_5), .in6(_6), .in7(_7), .in8(_8), .in9(_9),
    .in10(_10), .in11(_11), .in12(_12), .in13(_13), .in14(_14), .in15(_15), .in16(_16), .in17(_17),
    .in18(_18), .in19(_19), .in20(_20), .in21(_21), .in22(_22), .in23(_23), .in24(_24), .in25(_25),
    .in26(_26), .in27(_27), .in28(_28), .in29(_29), .in30(_30), .in31(_31), .out(Read_Data_1),
    .sel(Read_Register_1));  // open: en
  Multiplexer #(.select(5), .width(32)) multiplexer_2 (
    .in0(_0), .in1(_1), .in2(_2), .in3(_3), .in4(_4), .in5(_5), .in6(_6), .in7(_7), .in8(_8), .in9(_9),
    .in10(_10), .in11(_11), .in12(_12), .in13(_13), .in14(_14), .in15(_15), .in16(_16), .in17(_17),
    .in18(_18), .in19(_19), .in20(_20), .in21(_21), .in22(_22), .in23(_23), .in24(_24), .in25(_25),
    .in26(_26), .in27(_27), .in28(_28), .in29(_29), .in30(_30), .in31(_31), .out(Read_Data_2),
    .sel(Read_Register_2));  // open: en

  // Other names for the same wires on the sheet: RR1[4:0] = Read_Register_1; RR2[4:0] = Read_Register_2;
  //   WR[31:0] = Write_Data
endmodule

module Sign_Extend (
  input  [15:0] Input,
  output [31:0] Output
);


  assign Output = {{17{Input[15]}}, Input[14:0]};
endmodule

module Shift_left_2 (
  input  [31:0] Input,
  output [31:0] Output
);


  assign Output = {Input[29:0], 2'b00};
endmodule

module Procesador (
  input  in_1
);

  wire alu_32_bits_1_cero, ALUsrc, and_2_out, Branch, clock, clock_1_out, decodificador_instruccion_1_out_2,
       jr, jump, link, MemRead, MemtoReg, MemWrite, RegDst, RegWrite;
  wire [1:0] OP;
  wire [2:0] alu_control_1_alu_operation;
  wire [4:0] multiplexer_1_out, multiplexer_2_out;
  wire [5:0] _0_5;
  wire [23:0] divisor_por_4_1_output, divisor_por_4_2_output;
  wire [27:0] shift_left_2_28_1_output;
  wire [31:0] adder_2_out, alu_32_bits_1_alu_result, join_1_out_3, multiplexer_3_out, multiplexer_4_out,
       multiplexer_5_out, multiplexer_6_out, multiplexer_7_out, multiplexer_8_out, pc_4, ram_1_data,
       register_1_q, Rs, shift_left_2_1_output, sign_extend_1_output, Write;
  wire [31:6] Instruccion;

  Clock clock_1 (.out(clock_1_out));
  decodificador__Instruccion decodificador_instruccion_1 (
    .in_1({Instruccion, _0_5}), .out_2(decodificador_instruccion_1_out_2));
  Register #(.width(32)) register_1 (.D(multiplexer_7_out), .Q(register_1_q), .clk(clock), .clr(in_1));  // open: en
  and and_1 (clock, clock_1_out, ~decodificador_instruccion_1_out_2);  // AND_Gate
  Divisor_por_4 divisor_por_4_1 (.Input(register_1_q), .Output(divisor_por_4_1_output));
  decodificador_jr decodificador_jr_1 (.OP(OP), .funcion(_0_5), .Jr(jr));
  Adder #(.width(32)) adder_1 (.a(32'h4), .b(register_1_q), .out(pc_4));  // open: cin, cout
  ROM #(.addrWidth(24), .dataWidth(32)) rom_1 (.addr(divisor_por_4_1_output), .data({Instruccion, _0_5}));  // open: sel
  Shift_left_2__28 shift_left_2_28_1 (.Input({Instruccion[25:6], _0_5}), .Output(shift_left_2_28_1_output));
  Control control_1 (
    .Op_Code(Instruccion[31:26]), .RegDst(RegDst), .ALUScr(ALUsrc), .MemtoReg(MemtoReg), .RegWrite(RegWrite),
    .MemRead(MemRead), .MemWrite(MemWrite), .Branch(Branch), .ALU_Op(OP), .jump(jump), .link(link));
  Multiplexer #(.width(5)) multiplexer_1 (
    .in0(Instruccion[20:16]), .in1(Instruccion[15:11]), .out(multiplexer_1_out), .sel(RegDst));  // open: en
  Sign_Extend sign_extend_1 (.Input({Instruccion[15:6], _0_5}), .Output(sign_extend_1_output));
  Join join_1 (.in_1(shift_left_2_28_1_output), .in_2(pc_4[31:28]), .out_3(join_1_out_3));
  Multiplexer #(.width(5)) multiplexer_2 (
    .in0(multiplexer_1_out), .in1({5{1'b1}}), .out(multiplexer_2_out), .sel(link));  // open: en
  Multiplexer #(.width(32)) multiplexer_3 (
    .in0(multiplexer_8_out), .in1(pc_4), .out(multiplexer_3_out), .sel(link));  // open: en
  Shift_left_2 shift_left_2_1 (.Input(sign_extend_1_output), .Output(shift_left_2_1_output));
  Banco_de_Registros banco_de_registros_1 (
    .Read_Register_1(Instruccion[25:21]), .Read_Register_2(Instruccion[20:16]),
    .Write_Reg(multiplexer_2_out), .Write_Data(multiplexer_3_out), .Clock(clock), .Read_Data_1(Rs),
    .Read_Data_2(Write), .Reg_Write(RegWrite), .Reset(in_1));
  Adder #(.width(32)) adder_2 (.a(pc_4), .b(shift_left_2_1_output), .out(adder_2_out));  // open: cin, cout
  Multiplexer #(.width(32)) multiplexer_4 (
    .in0(Write), .in1(sign_extend_1_output), .out(multiplexer_4_out), .sel(ALUsrc));  // open: en
  ALU_Control alu_control_1 (.Funcion(_0_5), .OP(OP), .ALU_operation(alu_control_1_alu_operation));
  and and_2 (and_2_out, Branch, alu_32_bits_1_cero);
  ALU_32_bits alu_32_bits_1 (
    .Cero(alu_32_bits_1_cero), .ALU_Result(alu_32_bits_1_alu_result), .A(Rs), .B(multiplexer_4_out),
    .ALU_operacion(alu_control_1_alu_operation));
  Multiplexer #(.width(32)) multiplexer_5 (
    .in0(pc_4), .in1(adder_2_out), .out(multiplexer_5_out), .sel(and_2_out));  // open: en
  Divisor_por_4 divisor_por_4_2 (.Input(alu_32_bits_1_alu_result), .Output(divisor_por_4_2_output));
  Multiplexer #(.width(32)) multiplexer_6 (
    .in0(multiplexer_5_out), .in1(join_1_out_3), .out(multiplexer_6_out), .sel(jump));  // open: en
  Multiplexer #(.width(32)) multiplexer_7 (
    .in0(multiplexer_6_out), .in1(Rs), .out(multiplexer_7_out), .sel(jr));  // open: en
  RAM #(.addrWidth(24), .dataWidth(32), .bus("separate")) ram_1 (
    .addr(divisor_por_4_2_output), .din(Write), .data(ram_1_data), .str(MemWrite), .clk(clock), .ld(MemRead),
    .clr(in_1));  // open: sel
  Multiplexer #(.width(32)) multiplexer_8 (
    .in0(alu_32_bits_1_alu_result), .in1(ram_1_data), .out(multiplexer_8_out), .sel(MemtoReg));  // open: en

  // Other names for the same wires on the sheet: Instruccion[5:0] = _0_5; Reset = in_1

  // Notes on the sheet:
  //   contents of rom_1 (hex, n*v repeats v):
  //   2020 c000005 200500c8 c000015 0 20080030 4820 200a0001 200b0002 ac890000 ac8a0004 20840008 11680007
  //   a6020 1495020 c4820 ac8a0000 20840004 216b0001 800000c 3e00008 20100032 20110001 9020 9820 20140003
  //   acb10000 acb20004 acb30008 20a5000c 12900008 251a820 128820 139020 159820 acb50000 20a50004 22940001
  //   800001e 3e00008
endmodule

module Shift_left_2__28 (
  input  [25:0] Input,
  output [27:0] Output
);


  assign Output = {Input, 2'b00};
endmodule

module Join (
  input  [27:0] in_1,
  input  [3:0] in_2,
  output [31:0] out_3
);


  assign out_3 = {in_2, in_1};
endmodule

module Divisor_por_4 (
  input  [31:0] Input,
  output [23:0] Output
);


  assign Output = Input[25:2];
endmodule

module decodificador_jr (
  input  [1:0] OP,
  input  [5:0] funcion,
  output Jr
);

  wire and_1_out, and_2_out;

  and and_1 (and_1_out, OP[1], ~OP[0]);  // AND_Gate
  and and_2 (and_2_out, ~funcion[5], ~funcion[4], funcion[3], ~funcion[2], ~funcion[1], ~funcion[0]);  // AND_Gate
  and and_3 (Jr, and_1_out, and_2_out);
endmodule

module decodificador__Instruccion (
  input  [31:0] in_1,
  output out_2
);

  nor nor_1 (out_2, in_1[0], in_1[1], in_1[2], in_1[3], in_1[4], in_1[5], in_1[6], in_1[7], in_1[8], in_1[9], in_1[10], in_1[11], in_1[12], in_1[13], in_1[14], in_1[15], in_1[16], in_1[17], in_1[18], in_1[19], in_1[20], in_1[21], in_1[22], in_1[23], in_1[24], in_1[25], in_1[26], in_1[27], in_1[28], in_1[29], in_1[30], in_1[31]);
endmodule
