// Logisim project VideoJuego.circ as structural Verilog: 18 circuits, main circuit main
module main (
);

  wire a, b, c, clock_1_out, d, e, f, g, nuevo_juego;
  wire [1:0] control_1_out_36, joys;
  wire [31:0] control_1_out_4, control_1_out_5, control_1_out_6, control_1_out_7, control_1_out_8,
       control_1_out_9, control_1_out_10, control_1_out_11, control_1_out_12, control_1_out_13,
       control_1_out_14, control_1_out_15, control_1_out_16, control_1_out_17, control_1_out_18,
       control_1_out_19, control_1_out_20, control_1_out_21, control_1_out_22, control_1_out_23,
       control_1_out_24, control_1_out_25, control_1_out_26, control_1_out_27, control_1_out_28,
       control_1_out_29, control_1_out_30, control_1_out_31, control_1_out_32, control_1_out_33,
       control_1_out_34, control_1_out_35;

  Clock clock_1 (.out(clock_1_out));
  control control_1 (
    .nuevo(nuevo_juego), .joys(joys), .reloj(clock_1_out), .out_4(control_1_out_4), .out_5(control_1_out_5),
    .out_6(control_1_out_6), .out_7(control_1_out_7), .out_8(control_1_out_8), .out_9(control_1_out_9),
    .out_10(control_1_out_10), .out_11(control_1_out_11), .out_12(control_1_out_12),
    .out_13(control_1_out_13), .out_14(control_1_out_14), .out_15(control_1_out_15),
    .out_16(control_1_out_16), .out_17(control_1_out_17), .out_18(control_1_out_18),
    .out_19(control_1_out_19), .out_20(control_1_out_20), .out_21(control_1_out_21),
    .out_22(control_1_out_22), .out_23(control_1_out_23), .out_24(control_1_out_24),
    .out_25(control_1_out_25), .out_26(control_1_out_26), .out_27(control_1_out_27),
    .out_28(control_1_out_28), .out_29(control_1_out_29), .out_30(control_1_out_30),
    .out_31(control_1_out_31), .out_32(control_1_out_32), .out_33(control_1_out_33),
    .out_34(control_1_out_34), .out_35(control_1_out_35), .out_36(control_1_out_36));
  DotMatrix #(.inputtype("row"), .matrixcols(32), .matrixrows(32)) dotmatrix_1 (
    .row0(control_1_out_4), .row1(control_1_out_5), .row2(control_1_out_6), .row3(control_1_out_7),
    .row4(control_1_out_8), .row5(control_1_out_9), .row6(control_1_out_10), .row7(control_1_out_11),
    .row8(control_1_out_12), .row9(control_1_out_13), .row10(control_1_out_14), .row11(control_1_out_15),
    .row12(control_1_out_16), .row13(control_1_out_17), .row14(control_1_out_18), .row15(control_1_out_19),
    .row16(control_1_out_20), .row17(control_1_out_21), .row18(control_1_out_22), .row19(control_1_out_23),
    .row20(control_1_out_24), .row21(control_1_out_25), .row22(control_1_out_26), .row23(control_1_out_27),
    .row24(control_1_out_28), .row25(control_1_out_29), .row26(control_1_out_30), .row27(control_1_out_31),
    .row28(control_1_out_32), .row29(control_1_out_33), .row30(control_1_out_34), .row31(control_1_out_35));
  visualizador_vidas visualizador_vidas_1 (
    .b1(control_1_out_36[1]), .b0(control_1_out_36[0]), .a(a), .b(b), .c(c), .d(d), .e(e), .f(f), .g(g));
  Joystick #(.bits(2)) joystick_1 (.x(joys));  // open: y
  Button button_1 (.out(nuevo_juego));
  _7_Segment_Display u_7_segment_display_1 (.g(g), .f(f), .a(a), .b(b), .e(e), .d(d), .c(c));  // open: dp

  // Notes on the sheet:
  //   VIDAS
endmodule

module Decodificador_Joystick (
  input  J1,
  input  J0,
  output S,
  output R
);

  and and_1 (S, J1, J0);
  not not_1 (R, J1);
endmodule

module Reegistro_de_desplazamiento_8 (
  input  [31:0] fila,
  input  Reloj,
  input  limpiar,
  output [31:0] out_4,
  output [31:0] out_5,
  output [31:0] out_6,
  output [31:0] out_7,
  output [31:0] out_8,
  output [31:0] out_9,
  output [31:0] out_10,
  output [31:0] out_11
);

  Register #(.width(32)) register_1 (.D(fila), .Q(out_4), .clk(Reloj), .clr(limpiar));  // open: en
  Register #(.width(32)) register_2 (.D(out_4), .Q(out_5), .clk(Reloj), .clr(limpiar));  // open: en
  Register #(.width(32)) register_3 (.D(out_5), .Q(out_6), .clk(Reloj), .clr(limpiar));  // open: en
  Register #(.width(32)) register_4 (.D(out_6), .Q(out_7), .clk(Reloj), .clr(limpiar));  // open: en
  Register #(.width(32)) register_5 (.D(out_7), .Q(out_8), .clk(Reloj), .clr(limpiar));  // open: en
  Register #(.width(32)) register_6 (.D(out_8), .Q(out_9), .clk(Reloj), .clr(limpiar));  // open: en
  Register #(.width(32)) register_7 (.D(out_9), .Q(out_10), .clk(Reloj), .clr(limpiar));  // open: en
  Register #(.width(32)) register_8 (.D(out_10), .Q(out_11), .clk(Reloj), .clr(limpiar));  // open: en

  // Other names for the same wires on the sheet: c = Reloj
endmodule

// Registro desplazamiento
module Registro_de_desplazamiento_32 (
  input  [31:0] fila,
  input  Reloj,
  input  limpiar,
  output [31:0] out_4,
  output [31:0] out_5,
  output [31:0] out_6,
  output [31:0] out_7,
  output [31:0] out_8,
  output [31:0] out_9,
  output [31:0] out_10,
  output [31:0] out_11,
  output [31:0] out_12,
  output [31:0] out_13,
  output [31:0] out_14,
  output [31:0] out_15,
  output [31:0] out_16,
  output [31:0] out_17,
  output [31:0] out_18,
  output [31:0] out_19,
  output [31:0] out_20,
  output [31:0] out_21,
  output [31:0] out_22,
  output [31:0] out_23,
  output [31:0] out_24,
  output [31:0] out_25,
  output [31:0] out_26,
  output [31:0] out_27,
  output [31:0] out_28,
  output [31:0] out_29,
  output [31:0] out_30,
  output [31:0] out_31,
  output [31:0] out_32,
  output [31:0] out_33,
  output [31:0] out_34,
  output [31:0] out_35
);

  Reegistro_de_desplazamiento_8 reegistro_de_desplazamiento_8_1 (
    .fila(fila), .Reloj(Reloj), .limpiar(limpiar), .out_4(out_4), .out_5(out_5), .out_6(out_6),
    .out_7(out_7), .out_8(out_8), .out_9(out_9), .out_10(out_10), .out_11(out_11));
  Reegistro_de_desplazamiento_8 reegistro_de_desplazamiento_8_2 (
    .fila(out_11), .Reloj(Reloj), .limpiar(limpiar), .out_4(out_12), .out_5(out_13), .out_6(out_14),
    .out_7(out_15), .out_8(out_16), .out_9(out_17), .out_10(out_18), .out_11(out_19));
  Reegistro_de_desplazamiento_8 reegistro_de_desplazamiento_8_3 (
    .fila(out_19), .Reloj(Reloj), .limpiar(limpiar), .out_4(out_20), .out_5(out_21), .out_6(out_22),
    .out_7(out_23), .out_8(out_24), .out_9(out_25), .out_10(out_26), .out_11(out_27));
  Reegistro_de_desplazamiento_8 reegistro_de_desplazamiento_8_4 (
    .fila(out_27), .Reloj(Reloj), .limpiar(limpiar), .out_4(out_28), .out_5(out_29), .out_6(out_30),
    .out_7(out_31), .out_8(out_32), .out_9(out_33), .out_10(out_34), .out_11(out_35));

  // Other names for the same wires on the sheet: c = Reloj
endmodule

module Divisor_de_frecuencia (
  input  in_1,
  output out_2
);

  wire contador_2bits_1_y0, contador_2bits_1_y1;

  Contador_2bits contador_2bits_1 (
    .suma(1'b1), .reloj(in_1), .resta(1'b0), .clear(1'b0), .y1(contador_2bits_1_y1), .y0(contador_2bits_1_y0));
  and and_1 (out_2, contador_2bits_1_y1, contador_2bits_1_y0);
endmodule

module Colision (
  input  [31:0] in_1,
  input  [31:0] in_2,
  output out_3
);

  wire comparator_1_eq;
  wire [31:0] and_1_out;

  assign and_1_out = in_1 & in_2;  // AND_Gate and_1, 32 bits wide
  Comparator #(.width(32)) comparator_1 (.a(and_1_out), .b({32{1'b0}}), .eq(comparator_1_eq));  // open: gt, lt
  not not_1 (out_3, comparator_1_eq);
endmodule

// cursor
module Cursor_acoplado (
  input  [31:0] fila_1_obstaculos,
  input  [31:0] fila_2_obstaculos,
  input  [31:0] fila_3_obstaculos,
  input  [31:0] fila_4_obstaculos,
  input  [31:0] fila_5_obstaculos,
  input  [4:0] in_6,
  output [31:0] out_7,
  output [31:0] out_8,
  output [31:0] out_9,
  output [31:0] out_10,
  output [31:0] out_11,
  output out_12
);

  wire colision_2_out_3, colision_3_out_3, colision_out_3;
  wire [31:0] fila_1_out_2, fila_2_out, fila_3_out_2, fila_4_out, fila_5_out_2;

  Cursor_fila_1 fila_1 (.in_1(in_6), .out_2(fila_1_out_2));
  Cursor_fila_3 fila_3 (.in_1(in_6), .out_2(fila_3_out_2));
  Cursor_fila5 fila_5 (.in_1(in_6), .out_2(fila_5_out_2));
  assign fila_2_out = fila_1_out_2 | fila_5_out_2;  // OR_Gate fila_2, 32 bits wide
  assign fila_4_out = fila_1_out_2 | fila_5_out_2;  // OR_Gate fila_4, 32 bits wide
  Colision colision (.in_1(fila_1_obstaculos), .in_2(fila_1_out_2), .out_3(colision_out_3));
  Colision colision_2 (.in_1(fila_2_obstaculos), .in_2(fila_2_out), .out_3(colision_2_out_3));
  Colision colision_3 (.in_1(fila_3_obstaculos), .in_2(fila_3_out_2), .out_3(colision_3_out_3));
  assign out_9 = fila_3_obstaculos | fila_3_out_2;  // OR_Gate or_1, 32 bits wide
  or or_2 (out_12, colision_out_3, colision_2_out_3, colision_3_out_3);
  assign out_7 = fila_1_obstaculos | fila_1_out_2;  // OR_Gate or_3, 32 bits wide
  assign out_8 = fila_2_obstaculos | fila_2_out;  // OR_Gate or_4, 32 bits wide
  assign out_10 = fila_4_obstaculos | fila_4_out;  // OR_Gate or_5, 32 bits wide
  assign out_11 = fila_5_out_2 | fila_5_obstaculos;  // OR_Gate or_6, 32 bits wide
endmodule

module Cursor_fila5 (
  input  [4:0] in_1,
  output [31:0] out_2
);

  wire [30:3] decoder_1_out27;

  Decoder #(.select(5)) decoder_1 (
    .out0(decoder_1_out27[30]), .out1(decoder_1_out27[29]), .out2(decoder_1_out27[28]),
    .out3(decoder_1_out27[27]), .out4(decoder_1_out27[26]), .out5(decoder_1_out27[25]),
    .out6(decoder_1_out27[24]), .out7(decoder_1_out27[23]), .out8(decoder_1_out27[22]),
    .out9(decoder_1_out27[21]), .out10(decoder_1_out27[20]), .out11(decoder_1_out27[19]),
    .out12(decoder_1_out27[18]), .out13(decoder_1_out27[17]), .out14(decoder_1_out27[16]),
    .out15(decoder_1_out27[15]), .out16(decoder_1_out27[14]), .out17(decoder_1_out27[13]),
    .out18(decoder_1_out27[12]), .out19(decoder_1_out27[11]), .out20(decoder_1_out27[10]),
    .out21(decoder_1_out27[9]), .out22(decoder_1_out27[8]), .out23(decoder_1_out27[7]),
    .out24(decoder_1_out27[6]), .out25(decoder_1_out27[5]), .out26(decoder_1_out27[4]),
    .out27(decoder_1_out27[3]), .sel(in_1));  // open: out28, out29, out30, out31, en
  assign out_2 = {3'b000, decoder_1_out27, 1'b0} | {1'b0, decoder_1_out27, 3'b000};  // OR_Gate or_1, 32 bits wide
endmodule

module Cursor_fila_1 (
  input  [4:0] in_1,
  output [31:0] out_2
);

  Decoder #(.select(5)) decoder_1 (
    .out0(out_2[29]), .out1(out_2[28]), .out2(out_2[27]), .out3(out_2[26]), .out4(out_2[25]),
    .out5(out_2[24]), .out6(out_2[23]), .out7(out_2[22]), .out8(out_2[21]), .out9(out_2[20]),
    .out10(out_2[19]), .out11(out_2[18]), .out12(out_2[17]), .out13(out_2[16]), .out14(out_2[15]),
    .out15(out_2[14]), .out16(out_2[13]), .out17(out_2[12]), .out18(out_2[11]), .out19(out_2[10]),
    .out20(out_2[9]), .out21(out_2[8]), .out22(out_2[7]), .out23(out_2[6]), .out24(out_2[5]),
    .out25(out_2[4]), .out26(out_2[3]), .out27(out_2[2]), .sel(in_1));  // open: out28, out29, out30, out31, en

  assign {out_2[31:30], out_2[1:0]} = 4'b0000;
endmodule

module Cursor_fila_3 (
  input  [4:0] in_1,
  output [31:0] out_2
);

  wire [31:2] decoder_1_out27;

  Decoder #(.select(5)) decoder_1 (
    .out0(decoder_1_out27[31]), .out1(decoder_1_out27[30]), .out2(decoder_1_out27[27]),
    .out3(decoder_1_out27[26]), .out4(decoder_1_out27[25]), .out5(decoder_1_out27[24]),
    .out6(decoder_1_out27[23]), .out7(decoder_1_out27[22]), .out8(decoder_1_out27[21]),
    .out9(decoder_1_out27[20]), .out10(decoder_1_out27[19]), .out11(decoder_1_out27[18]),
    .out12(decoder_1_out27[17]), .out13(decoder_1_out27[16]), .out14(decoder_1_out27[15]),
    .out15(decoder_1_out27[14]), .out16(decoder_1_out27[13]), .out17(decoder_1_out27[12]),
    .out18(decoder_1_out27[11]), .out19(decoder_1_out27[10]), .out20(decoder_1_out27[9]),
    .out21(decoder_1_out27[8]), .out22(decoder_1_out27[7]), .out23(decoder_1_out27[6]),
    .out24(decoder_1_out27[5]), .out25(decoder_1_out27[4]), .out26(decoder_1_out27[3]),
    .out27(decoder_1_out27[2]), .sel(in_1));  // open: out28, out29, out30, out31, en
  assign out_2 = {4'b0000, decoder_1_out27[31:30], decoder_1_out27[27:2]} | {decoder_1_out27[31:30], decoder_1_out27[31:30], decoder_1_out27[27:2], 2'b00} | {decoder_1_out27[31:30], decoder_1_out27[27:2], 4'b0000};  // OR_Gate or_1, 32 bits wide
endmodule

// 2 bits
module Contador_2bits (
  input  suma,
  input  reloj,
  input  resta,
  input  clear,
  output y1,
  output y0
);

  wire and_1_out, and_2_out, or_1_out, xor_1_out;

  xor xor_1 (xor_1_out, suma, resta);
  and and_1 (and_1_out, ~y0, ~suma, resta);  // AND_Gate
  or or_1 (or_1_out, and_1_out, and_2_out);
  and and_2 (and_2_out, y0, suma, ~resta);  // AND_Gate
  J_K_Flip_Flop ff_0 (.J(xor_1_out), .clk(reloj), .K(xor_1_out), .Q(y0), .reset(clear));  // open: Qn, preset, en
  J_K_Flip_Flop ff_1 (.J(or_1_out), .clk(reloj), .K(or_1_out), .Q(y1), .reset(clear));  // open: Qn, preset, en

  // Other names for the same wires on the sheet: cl = reloj; rst = clear
endmodule

module Contador_4_bits (
  input  suma,
  input  reloj,
  input  resta,
  input  reset,
  output out_5,
  output out_6,
  output out_7,
  output out_8
);

  wire and_1_out, and_2_out, and_3_out, nor_1_out;

  nor nor_1 (nor_1_out, out_7, out_8);
  and and_1 (and_1_out, nor_1_out, resta);
  and and_2 (and_2_out, out_7, out_8);
  and and_3 (and_3_out, and_2_out, suma);
  Contador_2bits contador_2bits_1 (.suma(suma), .reloj(reloj), .resta(resta), .clear(reset), .y1(out_7), .y0(out_8));
  Contador_2bits contador_2bits_2 (
    .suma(and_3_out), .reloj(reloj), .resta(and_1_out), .clear(reset), .y1(out_5), .y0(out_6));

  // Other names for the same wires on the sheet: add = suma; b0 = out_5; b1 = out_6; b2 = out_7; b3 = out_8;
  //   reduce = resta
endmodule

module Contador_cursor (
  input  suma,
  input  reloj,
  input  resta,
  output [4:0] out_4
);

  wire and_1_out, and_2_out, or_1_out, or_2_out;

  or or_1 (or_1_out, ~out_4[4], ~out_4[3], out_4[2], ~out_4[1], ~out_4[0]);  // OR_Gate
  or or_2 (or_2_out, out_4[4], out_4[3], out_4[2], out_4[1], out_4[0]);
  and and_1 (and_1_out, or_1_out, suma);
  and and_2 (and_2_out, resta, or_2_out);
  Contador_5_bits contador_5_bits_1 (.suma(and_1_out), .reloj(reloj), .resta(and_2_out), .reset(1'b0), .out_5(out_4));

  // Other names for the same wires on the sheet: b4 = out_4[0]; b3 = out_4[1]; b2 = out_4[2]; b1 = out_4[3];
  //   b0 = out_4[4]
endmodule

// Control juego
module control (
  input  nuevo,
  input  [1:0] joys,
  input  reloj,
  output [31:0] out_4,
  output [31:0] out_5,
  output [31:0] out_6,
  output [31:0] out_7,
  output [31:0] out_8,
  output [31:0] out_9,
  output [31:0] out_10,
  output [31:0] out_11,
  output [31:0] out_12,
  output [31:0] out_13,
  output [31:0] out_14,
  output [31:0] out_15,
  output [31:0] out_16,
  output [31:0] out_17,
  output [31:0] out_18,
  output [31:0] out_19,
  output [31:0] out_20,
  output [31:0] out_21,
  output [31:0] out_22,
  output [31:0] out_23,
  output [31:0] out_24,
  output [31:0] out_25,
  output [31:0] out_26,
  output [31:0] out_27,
  output [31:0] out_28,
  output [31:0] out_29,
  output [31:0] out_30,
  output [31:0] out_31,
  output [31:0] out_32,
  output [31:0] out_33,
  output [31:0] out_34,
  output [31:0] out_35,
  output [1:0] out_36
);

  wire c4, clear, Deco_Joystick_r, Deco_Joystick_s, decoder_1_out1, decoder_1_out2, decoder_1_out3, or_1_out,
       or_2_out, or_3_out, r, Reiniciar;
  wire [4:0] Cont_cursor_out_4;
  wire [5:0] contador_6_bits_1_out_5;
  wire [31:0] multiplexer_1_out, registro_de_desplazamiento_32_1_out_31,
       registro_de_desplazamiento_32_1_out_32, registro_de_desplazamiento_32_1_out_33,
       registro_de_desplazamiento_32_1_out_34, registro_de_desplazamiento_32_1_out_35, rom_1_data,
       rom_2_data, rom_3_data;

  or or_1 (or_1_out, r, Reiniciar);
  Contador_6_bits contador_6_bits_1 (
    .suma(1'b1), .reloj(c4), .resta(1'b0), .reset(or_1_out), .out_5(contador_6_bits_1_out_5));
  Decoder #(.select(2)) decoder_1 (
    .out0(clear), .out1(decoder_1_out1), .out2(decoder_1_out2), .out3(decoder_1_out3), .sel(out_36));  // open: en
  Decodificador_Joystick Deco_Joystick (.J1(joys[1]), .J0(joys[0]), .S(Deco_Joystick_s), .R(Deco_Joystick_r));
  and and_1 (Reiniciar, clear, nuevo);
  Contador_cursor Cont_cursor (
    .suma(Deco_Joystick_s), .reloj(reloj), .resta(Deco_Joystick_r), .out_4(Cont_cursor_out_4));
  Divisor_de_frecuencia Divisor_Frecuencia (.in_1(reloj), .out_2(c4));
  ROM #(.addrWidth(6), .dataWidth(32)) rom_1 (.addr(contador_6_bits_1_out_5), .data(rom_1_data), .sel(decoder_1_out1));
  ROM #(.addrWidth(6), .dataWidth(32)) rom_2 (.addr(contador_6_bits_1_out_5), .data(rom_2_data), .sel(decoder_1_out2));
  ROM #(.addrWidth(6), .dataWidth(32)) rom_3 (.addr(contador_6_bits_1_out_5), .data(rom_3_data), .sel(decoder_1_out3));
  Multiplexer #(.select(2), .width(32)) multiplexer_1 (
    .in1(rom_1_data), .in2(rom_2_data), .in3(rom_3_data), .out(multiplexer_1_out), .sel(out_36));  // open: in0, en
  or or_2 (or_2_out, r, clear);
  Registro_de_desplazamiento_32 registro_de_desplazamiento_32_1 (
    .fila(multiplexer_1_out), .Reloj(c4), .limpiar(or_2_out), .out_4(out_4), .out_5(out_5), .out_6(out_6),
    .out_7(out_7), .out_8(out_8), .out_9(out_9), .out_10(out_10), .out_11(out_11), .out_12(out_12),
    .out_13(out_13), .out_14(out_14), .out_15(out_15), .out_16(out_16), .out_17(out_17), .out_18(out_18),
    .out_19(out_19), .out_20(out_20), .out_21(out_21), .out_22(out_22), .out_23(out_23), .out_24(out_24),
    .out_25(out_25), .out_26(out_26), .out_27(out_27), .out_28(out_28), .out_29(out_29), .out_30(out_30),
    .out_31(registro_de_desplazamiento_32_1_out_31), .out_32(registro_de_desplazamiento_32_1_out_32),
    .out_33(registro_de_desplazamiento_32_1_out_33), .out_34(registro_de_desplazamiento_32_1_out_34),
    .out_35(registro_de_desplazamiento_32_1_out_35));
  Cursor_acoplado cursor_acoplado_1 (
    .fila_1_obstaculos(registro_de_desplazamiento_32_1_out_31),
    .fila_2_obstaculos(registro_de_desplazamiento_32_1_out_32),
    .fila_3_obstaculos(registro_de_desplazamiento_32_1_out_33),
    .fila_4_obstaculos(registro_de_desplazamiento_32_1_out_34),
    .fila_5_obstaculos(registro_de_desplazamiento_32_1_out_35), .in_6(Cont_cursor_out_4), .out_7(out_31),
    .out_8(out_32), .out_9(out_33), .out_10(out_34), .out_11(out_35), .out_12(r));
  or or_3 (or_3_out, r, Reiniciar);
  Contador_2bits contador_2bits_1 (
    .suma(1'b0), .reloj(or_3_out), .resta(1'b1), .clear(1'b0), .y1(out_36[1]), .y0(out_36[0]));

  // Other names for the same wires on the sheet: Vidas[1:0] = out_36

  // Notes on the sheet:
  //   contents of rom_1 (hex, n*v repeats v):
  //   100000 380000 100000 40000040 e00000e0 40000040 0 0 1000 81c03800 c0801000 80000000 44 4000028
  //   e0400fe 40e0054 40038 54 0 200 100700 380200 10100000 38000000 10000000 0 0 1001c 10008 38000 10000
  //   10000 100 380 440100 280000 40fe0000 e0540004 4038000e 540004 1004 3800 1000 0 38000000 7c000010
  //   c6000010 c6000010 fe010038 380380fe 92038 44010 28010 10010 0 2000000 7000000 2000000 22010 14038
  //   7f010 2002a000 7001c000 2002a000
  //   contents of rom_2 (hex, n*v repeats v):
  //   0 0 40008400 40004801 e0003003 40003007 480f 808407 1c00003 3e00001 7f00000 3e00000 1c00000 800000
  //   2000 2000 7000 2000 0 84000008 4800001c 3000003e 3000007f 4800003e 8400001c 8 8000 1c000 3e000 7f000
  //   3e000 1c000 8008000 1c000020 3e000070 7f0000f8 3e0001fc 1c0000f8 8020070 70020 f8000 1fc000 f8000
  //   70000 20000 0 8000000 1c000000 3e000108 7f010090 3e010060 1c038060 8010090 108 0 80000 801c0000
  //   c03e0001 e07f0003 f03e0207 e01c020f c0080707 80000203 1
  //   contents of rom_3 (hex, n*v repeats v):
  //   10000040 0 4000000 2000010 4000008 10 0 0 0 8000 10000 0 10000004 28000000 4*0 40000 0 100 280
  //   40040000 20000 40000 6*0 2001002 5002005 6*0 80000 40040 100800a0 7*0 10 0 0 80000000 40801000
  //   81002800
endmodule

module visualizador_vidas (
  input  b1,
  input  b0,
  output a,
  output b,
  output c,
  output d,
  output e,
  output f,
  output g
);

  wire not_1_out, not_2_out, not_3_out, not_5_out, not_6_out;

  not not_1 (not_1_out, b0);
  not not_2 (not_2_out, b1);
  not not_3 (not_3_out, b0);
  not not_4 (e, b0);
  not not_5 (not_5_out, b1);
  not not_6 (not_6_out, b0);
  or or_1 (a, not_1_out, b1);
  or or_2 (c, not_2_out, b0);
  or or_3 (d, not_3_out, b1);
  and and_1 (f, not_5_out, not_6_out);

  assign b = 1'b1;
  assign g = b1;
endmodule

module Contador_6_bits (
  input  suma,
  input  reloj,
  input  resta,
  input  reset,
  output [5:0] out_5
);

  wire and_1_out, and_2_out, and_3_out, and_4_out, nor_1_out, nor_2_out;

  nor nor_1 (nor_1_out, out_5[3], out_5[2]);
  nor nor_2 (nor_2_out, out_5[1], out_5[0]);
  and and_1 (and_1_out, nor_1_out, nor_2_out, resta);
  and and_2 (and_2_out, out_5[3], out_5[2]);
  and and_3 (and_3_out, out_5[1], out_5[0]);
  and and_4 (and_4_out, and_2_out, and_3_out, suma);
  Contador_2bits contador_2bits_1 (
    .suma(and_4_out), .reloj(reloj), .resta(and_1_out), .clear(reset), .y1(out_5[5]), .y0(out_5[4]));
  Contador_4_bits _4_bits_cont (
    .suma(suma), .reloj(reloj), .resta(resta), .reset(reset), .out_5(out_5[3]), .out_6(out_5[2]),
    .out_7(out_5[1]), .out_8(out_5[0]));

  // Other names for the same wires on the sheet: add = suma; b5 = out_5[0]; b4 = out_5[1]; b3 = out_5[2];
  //   b2 = out_5[3]; b1 = out_5[4]; b0 = out_5[5]; reduce = resta
endmodule

module Contador_5_bits (
  input  suma,
  input  reloj,
  input  resta,
  input  reset,
  output [4:0] out_5
);

  wire and_1_out, and_2_out, and_3_out, nor_1_out;

  nor nor_1 (nor_1_out, out_5[3], out_5[2], out_5[1], out_5[0]);
  and and_1 (and_1_out, nor_1_out, resta);
  and and_2 (and_2_out, out_5[3], out_5[2], out_5[1], out_5[0]);
  and and_3 (and_3_out, and_2_out, suma);
  contador_1_bit _1_bit_cont (.s(and_3_out), .reloj(reloj), .r(and_1_out), .out_5(out_5[4]));  // open: clear
  Contador_4_bits _4_bits_cont (
    .suma(suma), .reloj(reloj), .resta(resta), .reset(reset), .out_5(out_5[3]), .out_6(out_5[2]),
    .out_7(out_5[1]), .out_8(out_5[0]));

  // Other names for the same wires on the sheet: add = suma; b4 = out_5[0]; b3 = out_5[1]; b2 = out_5[2];
  //   b1 = out_5[3]; b0 = out_5[4]; reduce = resta
endmodule

module contador_1_bit (
  input  s,
  input  reloj,
  input  r,
  input  clear,
  output out_5
);

  wire and_1_out, and_2_out, and_3_out, and_4_out, not_1_out, not_2_out, not_3_out, not_4_out, or_1_out,
       or_2_out;

  not not_1 (not_1_out, s);
  not not_2 (not_2_out, r);
  not not_3 (not_3_out, s);
  not not_4 (not_4_out, r);
  and and_1 (and_1_out, not_1_out, r);
  and and_2 (and_2_out, s, not_2_out);
  and and_3 (and_3_out, not_3_out, r);
  and and_4 (and_4_out, s, not_4_out);
  or or_1 (or_1_out, and_1_out, and_2_out);
  or or_2 (or_2_out, and_3_out, and_4_out);
  J_K_Flip_Flop j_k_ff_1 (.J(or_1_out), .clk(reloj), .K(or_2_out), .Q(out_5), .reset(clear));  // open: Qn, preset, en

  // Other names for the same wires on the sheet: cl = reloj; rst = clear
endmodule
